// Digital circuit gaming pc.dig as structural Verilog
module gaming_pc (
  input  clk
);

  wire Address_Select, IP_Enable, IP_Write, Next_Instruction, RAM_Load, RAM_Store, Reg_A_Read, Reg_A_Write,
       Reg_B_Read, Reg_B_Write;
  wire [3:0] Stage_Counter_out;
  wire [7:0] _64kx8_RAM_d, Instruction_q, Register_A_q, Register_B_q;
  wire [12:7] Control_ROM_d;
  wire [15:0] IP_out, multiplexer_1_out;

  Register #(.Bits(8)) Register_A (.D(_64kx8_RAM_d), .C(clk), .en(Reg_A_Write), .Q(Register_A_q));
  Register #(.Bits(8)) Register_B (.D(_64kx8_RAM_d), .C(clk), .en(Reg_B_Write), .Q(Register_B_q));
  Register #(.Bits(8)) Instruction (.D(_64kx8_RAM_d), .C(clk), .en(Next_Instruction), .Q(Instruction_q));
  Counter #(.Bits(4)) Stage_Counter (.en(1'b1), .C(clk), .clr(Next_Instruction), .out(Stage_Counter_out));  // open: ovf
  CounterPreset #(.Bits(16)) IP (
    .en(IP_Enable), .C(clk), .dir(1'b0), .in({Register_B_q, Register_A_q}), .ld(IP_Write), .clr(1'b0),
    .out(IP_out));  // open: ovf
  // Probe Instruction on Instruction_q
  // Probe Stage on Stage_Counter_out
  Driver #(.Bits(8)) driver_1 (.in(Register_A_q), .en(Reg_A_Read));  // open: out
  Driver #(.Bits(8)) driver_2 (.in(Register_B_q), .en(Reg_B_Read));  // open: out
  Multiplexer #(.Bits(16)) multiplexer_1 (
    .sel(Address_Select), .in_0({Register_B_q, Register_A_q}), .in_1(IP_out), .out(multiplexer_1_out));
  ROM #(.AddrBits(12), .isProgramMemory("true"), .Bits(16)) Control_ROM (
    .A({Instruction_q, Stage_Counter_out}), .sel(1'b1),
    .D({Next_Instruction, IP_Enable, IP_Write, Control_ROM_d, Reg_B_Read, Reg_B_Write, Reg_A_Read, Reg_A_Write, RAM_Store, RAM_Load, Address_Select}));
  // Probe Address on multiplexer_1_out
  RAMSinglePort #(.AddrBits(16), .Bits(8)) _64kx8_RAM (
    .A(multiplexer_1_out), .str(RAM_Store), .C(clk), .ld(RAM_Load), .D(_64kx8_RAM_d));
  // Probe Bus on _64kx8_RAM_d

  // Notes on the sheet:
  //   contents of Control_ROM (hex, n*v repeats v):
  //   c003
  //   TODO
  //   - Stack pointer
  //   - up address mux to 3
  //   - put IP on address mux 0
endmodule
